// Logisim project Contador.circ as structural Verilog: 1 circuit, main circuit main
module main (
  input  B,
  input  C
);

  wire and_1_out, and_2_out, and_3_out, and_4_out, and_5_out, and_6_out, and_7_out, and_8_out, and_9_out,
       and_10_out, and_11_out, and_12_out, and_13_out, and_14_out, and_15_out, and_16_out, and_17_out,
       and_18_out, and_19_out, and_20_out, and_21_out, and_22_out, and_23_out, and_24_out, and_25_out,
       and_26_out, and_27_out, and_28_out, and_29_out, and_30_out, and_31_out, and_32_out, and_33_out,
       and_34_out, and_35_out, and_36_out, clock_1_out, j_k_ff_1_q, j_k_ff_2_q, j_k_ff_3_q, j_k_ff_4_q,
       nand_1_out, not_1_out, not_2_out, not_3_out, not_4_out, not_5_out, not_6_out, not_7_out, not_8_out,
       not_9_out, not_10_out, not_11_out, not_12_out, not_13_out, not_14_out, not_15_out, not_16_out,
       not_17_out, not_18_out, not_19_out, not_20_out, not_21_out, not_22_out, not_23_out, not_24_out,
       not_25_out, not_26_out, not_27_out, not_28_out, not_29_out, not_30_out, not_31_out, not_32_out,
       not_33_out, not_34_out, not_35_out, not_36_out, not_37_out, not_38_out, not_39_out, not_40_out,
       not_41_out, not_42_out, not_43_out, not_44_out, not_45_out, not_46_out, not_47_out, not_48_out,
       or_1_out, or_2_out, or_3_out, or_4_out, or_5_out, or_6_out, or_7_out;

  not not_1 (not_1_out, j_k_ff_2_q);
  J_K_Flip_Flop j_k_ff_1 (
    .J(1'b1), .clk(not_1_out), .K(1'b1), .Q(j_k_ff_1_q), .en(not_2_out));  // open: Qn, preset, reset
  not not_2 (not_2_out, nand_1_out);
  not not_3 (not_3_out, j_k_ff_3_q);
  J_K_Flip_Flop j_k_ff_2 (
    .J(1'b1), .clk(not_3_out), .K(1'b1), .Q(j_k_ff_2_q), .en(not_4_out));  // open: Qn, preset, reset
  not not_4 (not_4_out, nand_1_out);
  nand nand_1 (nand_1_out, B, C);
  not not_5 (not_5_out, j_k_ff_4_q);
  J_K_Flip_Flop j_k_ff_3 (
    .J(1'b1), .clk(not_5_out), .K(1'b1), .Q(j_k_ff_3_q), .en(not_6_out));  // open: Qn, preset, reset
  not not_6 (not_6_out, nand_1_out);
  not not_7 (not_7_out, clock_1_out);
  J_K_Flip_Flop j_k_ff_4 (
    .J(1'b1), .clk(not_7_out), .K(1'b1), .Q(j_k_ff_4_q), .en(not_8_out));  // open: Qn, preset, reset
  not not_8 (not_8_out, nand_1_out);
  Clock clock_1 (.out(clock_1_out));
  not not_9 (not_9_out, j_k_ff_2_q);
  not not_10 (not_10_out, j_k_ff_4_q);
  not not_11 (not_11_out, j_k_ff_1_q);
  not not_12 (not_12_out, j_k_ff_2_q);
  not not_13 (not_13_out, j_k_ff_3_q);
  not not_14 (not_14_out, j_k_ff_4_q);
  not not_15 (not_15_out, j_k_ff_1_q);
  not not_16 (not_16_out, j_k_ff_1_q);
  not not_17 (not_17_out, j_k_ff_2_q);
  not not_18 (not_18_out, j_k_ff_3_q);
  not not_19 (not_19_out, j_k_ff_4_q);
  not not_20 (not_20_out, j_k_ff_3_q);
  not not_21 (not_21_out, j_k_ff_2_q);
  not not_22 (not_22_out, j_k_ff_4_q);
  not not_23 (not_23_out, j_k_ff_3_q);
  not not_24 (not_24_out, j_k_ff_1_q);
  not not_25 (not_25_out, j_k_ff_2_q);
  not not_26 (not_26_out, j_k_ff_4_q);
  not not_27 (not_27_out, j_k_ff_1_q);
  not not_28 (not_28_out, j_k_ff_2_q);
  not not_29 (not_29_out, j_k_ff_4_q);
  not not_30 (not_30_out, j_k_ff_3_q);
  not not_31 (not_31_out, j_k_ff_2_q);
  not not_32 (not_32_out, j_k_ff_2_q);
  not not_33 (not_33_out, j_k_ff_4_q);
  not not_34 (not_34_out, j_k_ff_4_q);
  not not_35 (not_35_out, j_k_ff_3_q);
  not not_36 (not_36_out, j_k_ff_4_q);
  not not_37 (not_37_out, j_k_ff_1_q);
  not not_38 (not_38_out, j_k_ff_3_q);
  not not_39 (not_39_out, j_k_ff_2_q);
  not not_40 (not_40_out, j_k_ff_4_q);
  not not_41 (not_41_out, j_k_ff_1_q);
  not not_42 (not_42_out, j_k_ff_3_q);
  not not_43 (not_43_out, j_k_ff_2_q);
  not not_44 (not_44_out, j_k_ff_2_q);
  not not_45 (not_45_out, j_k_ff_4_q);
  and and_1 (and_1_out, not_9_out, not_10_out);
  and and_2 (and_2_out, not_11_out, j_k_ff_3_q);
  and and_3 (and_3_out, j_k_ff_2_q, j_k_ff_3_q);
  and and_4 (and_4_out, j_k_ff_1_q, not_12_out, not_13_out);
  and and_5 (and_5_out, j_k_ff_1_q, j_k_ff_2_q, not_14_out);
  and and_6 (and_6_out, not_15_out, j_k_ff_2_q, j_k_ff_4_q);
  and and_7 (and_7_out, not_16_out, not_17_out);
  and and_8 (and_8_out, not_16_out, not_18_out, not_19_out);
  and and_9 (and_9_out, not_16_out, j_k_ff_3_q, j_k_ff_4_q);
  and and_10 (and_10_out, j_k_ff_1_q, not_20_out, j_k_ff_4_q);
  and and_11 (and_11_out, not_21_out, not_22_out);
  not not_46 (not_46_out, j_k_ff_1_q);
  and and_12 (and_12_out, not_46_out, not_47_out);
  not not_47 (not_47_out, j_k_ff_3_q);
  and and_13 (and_13_out, not_46_out, j_k_ff_4_q);
  and and_14 (and_14_out, not_46_out, j_k_ff_2_q);
  and and_15 (and_15_out, not_47_out, j_k_ff_4_q);
  and and_16 (and_16_out, j_k_ff_1_q, not_48_out);
  not not_48 (not_48_out, j_k_ff_2_q);
  and and_17 (and_17_out, j_k_ff_1_q, not_23_out);
  and and_18 (and_18_out, not_24_out, not_25_out, not_26_out);
  and and_19 (and_19_out, not_27_out, not_28_out, j_k_ff_3_q);
  and and_20 (and_20_out, j_k_ff_2_q, j_k_ff_3_q, not_29_out);
  and and_21 (and_21_out, j_k_ff_2_q, not_30_out, j_k_ff_4_q);
  and and_22 (and_22_out, j_k_ff_1_q, not_31_out, j_k_ff_4_q);
  and and_23 (and_23_out, not_32_out, not_33_out);
  and and_24 (and_24_out, j_k_ff_1_q, j_k_ff_2_q);
  and and_25 (and_25_out, j_k_ff_3_q, not_34_out);
  and and_26 (and_26_out, j_k_ff_1_q, j_k_ff_3_q);
  and and_27 (and_27_out, not_35_out, not_36_out);
  and and_28 (and_28_out, not_37_out, j_k_ff_2_q, not_38_out);
  and and_29 (and_29_out, j_k_ff_1_q, not_39_out);
  and and_30 (and_30_out, j_k_ff_2_q, not_40_out);
  and and_31 (and_31_out, j_k_ff_1_q, j_k_ff_3_q);
  and and_32 (and_32_out, not_41_out, j_k_ff_2_q, not_42_out);
  and and_33 (and_33_out, j_k_ff_1_q, not_43_out);
  and and_34 (and_34_out, not_44_out, j_k_ff_3_q);
  and and_35 (and_35_out, j_k_ff_3_q, not_45_out);
  and and_36 (and_36_out, j_k_ff_1_q, j_k_ff_4_q);
  or or_1 (or_1_out, and_7_out, and_8_out, and_9_out, and_10_out, and_11_out);
  or or_2 (or_2_out, and_12_out, and_13_out, and_14_out, and_15_out, and_16_out);
  or or_3 (or_3_out, and_17_out, and_18_out, and_19_out, and_20_out, and_21_out, and_22_out);
  or or_4 (or_4_out, and_23_out, and_24_out, and_25_out, and_26_out);
  or or_5 (or_5_out, and_27_out, and_28_out, and_29_out, and_30_out, and_31_out);
  or or_6 (or_6_out, and_32_out, and_33_out, and_34_out, and_35_out, and_36_out);
  or or_7 (or_7_out, and_1_out, and_2_out, and_3_out, and_4_out, and_5_out, and_6_out);
  _7_Segment_Display u_7_segment_display_1 (
    .g(or_6_out), .f(or_5_out), .a(or_7_out), .b(or_1_out), .e(or_4_out), .d(or_3_out), .c(or_2_out));  // open: dp

  // Notes on the sheet:
  //   Contador
  //   A
  //   A
  //   A
  //   A
  //   A
  //   A
  //   B
  //   C
  //   D
  //   C
  //   B
  //   D
  //   C
  //   B
  //   C
  //   B
  //   B
  //   C
  //   B
  //   C
  //   D
  //   D
  //   D
  //   D
  //   Segmento B
  //   Segmento A
  //   Segmento C
  //   Segmento D
  //   Segmento E
  //   Segmento F
  //   Segmento G
endmodule
